// Logisim project CounterJohsonWithSelfCorrection.circ as structural Verilog: 1 circuit, main circuit main
module main (
);

  wire and_1_out, and_2_out, and_3_out, and_4_out, and_5_out, and_6_out, and_7_out, and_8_out, and_9_out,
       and_10_out, and_11_out, and_12_out, button_1_out, button_2_out, D0, D1, D2, nor_1_out, R0, R1, R2, R3,
       R4, S0, S1, S2, S4, S5;

  LED led_1 (.in(and_1_out));
  and and_1 (and_1_out, R0, R2);
  Button button_1 (.out(button_1_out));
  LED led_2 (.in(and_2_out));
  and and_2 (and_2_out, R3, D0);
  Button button_2 (.out(button_2_out));
  LED led_3 (.in(and_3_out));
  and and_3 (and_3_out, S0, R1);
  D_Flip_Flop d_ff_1 (.clk(button_1_out), .D(R2), .Q(S0), .Qn(R0));  // open: preset, reset
  LED led_4 (.in(and_4_out));
  and and_4 (and_4_out, D2, R4);
  D_Flip_Flop d_ff_2 (.clk(button_2_out), .D(D0), .Q(D2), .Qn(R3));  // open: preset, reset
  LED led_5 (.in(and_5_out));
  LED led_6 (.in(and_6_out));
  and and_5 (and_5_out, S1, R2);
  and and_6 (and_6_out, S0, S2);
  LED led_7 (.in(and_7_out));
  LED led_8 (.in(and_8_out));
  and and_7 (and_7_out, S4, D0);
  and and_8 (and_8_out, D2, S5);
  nor nor_1 (nor_1_out, S4, D0);
  LED led_9 (.in(and_9_out));
  and and_9 (and_9_out, S1, R0);
  D_Flip_Flop d_ff_3 (.clk(button_1_out), .D(S0), .Q(S1), .Qn(R1));  // open: preset, reset
  LED led_10 (.in(and_10_out));
  and and_10 (and_10_out, S4, R3);
  nor nor_2 (D1, R3, nor_1_out);
  D_Flip_Flop d_ff_4 (.clk(button_2_out), .D(D1), .Q(S4), .Qn(R4));  // open: preset, reset
  LED led_11 (.in(and_11_out));
  LED led_12 (.in(S0));
  and and_11 (and_11_out, S2, R1);
  LED led_13 (.in(S1));
  LED led_14 (.in(S2));
  D_Flip_Flop d_ff_5 (.clk(button_1_out), .D(S1), .Q(S2), .Qn(R2));  // open: preset, reset
  LED led_15 (.in(and_12_out));
  LED led_16 (.in(D2));
  and and_12 (and_12_out, S5, R4);
  LED led_17 (.in(S4));
  LED led_18 (.in(S5));
  D_Flip_Flop d_ff_6 (.clk(button_2_out), .D(D2), .Q(S5), .Qn(D0));  // open: preset, reset

  // Other names for the same wires on the sheet: R5 = D0; S3 = D2
endmodule
