// Logisim project CounterJohsons.circ as structural Verilog: 1 circuit, main circuit main
module main (
);

  wire A0, B0, button_1_out, button_2_out, button_3_out, button_4_out, button_5_out, button_6_out,
       button_7_out, button_8_out, button_9_out, button_10_out, button_11_out, button_12_out, C0, C1, D0, D1,
       E0, E1, E2, F0, F1, F2, G0, G1, G2, G3, H0, H1, H2, H3, I0, I1, I2, I3, I4, J0, J1, J2, J3, J4, K0,
       K1, K2, K3, K4, K5, L0, L1, L2, L3, L4, L5, nor_1_out, nor_2_out, nor_3_out, nor_4_out, nor_5_out,
       nor_6_out, nor_7_out, nor_8_out, nor_9_out, nor_10_out, nor_11_out, nor_12_out, nor_13_out,
       nor_14_out, nor_15_out, nor_16_out, nor_17_out, nor_18_out, nor_19_out, nor_20_out, nor_21_out,
       nor_22_out, nor_23_out, nor_24_out, nor_25_out, nor_26_out, nor_27_out, nor_28_out, nor_29_out,
       nor_30_out, nor_31_out, nor_32_out, nor_33_out, nor_34_out, nor_35_out, nor_36_out, nor_37_out,
       nor_38_out, nor_39_out, nor_40_out, nor_41_out, nor_42_out;

  Button button_1 (.out(button_1_out));
  Button button_2 (.out(button_2_out));
  Button button_3 (.out(button_3_out));
  Button button_4 (.out(button_4_out));
  LED led_1 (.in(nor_1_out));
  nor nor_1 (nor_1_out, E0, E2);
  Button button_5 (.out(button_5_out));
  Button button_6 (.out(button_6_out));
  LED led_2 (.in(nor_2_out));
  LED led_3 (.in(nor_3_out));
  nor nor_2 (nor_2_out, B0, B0);
  nor nor_3 (nor_3_out, A0, A0);
  D_Flip_Flop d_ff_1 (.clk(button_1_out), .D(B0), .Q(A0), .Qn(B0), .reset(button_2_out));  // open: preset
  LED led_4 (.in(nor_4_out));
  LED led_5 (.in(nor_5_out));
  nor nor_4 (nor_4_out, D0, C1);
  nor nor_5 (nor_5_out, C0, C1);
  D_Flip_Flop d_ff_2 (.clk(button_3_out), .D(D1), .Q(C0), .Qn(D0), .reset(button_4_out));  // open: preset
  LED led_6 (.in(nor_6_out));
  nor nor_6 (nor_6_out, F0, E1);
  D_Flip_Flop d_ff_3 (.clk(button_5_out), .D(F2), .Q(E0), .Qn(F0), .reset(button_6_out));  // open: preset
  LED led_7 (.in(nor_7_out));
  nor nor_7 (nor_7_out, D0, D1);
  LED led_8 (.in(nor_8_out));
  nor nor_8 (nor_8_out, E2, F1);
  LED led_9 (.in(nor_9_out));
  LED led_10 (.in(nor_10_out));
  nor nor_9 (nor_9_out, K0, K5);
  nor nor_10 (nor_10_out, L0, K1);
  Button button_7 (.out(button_7_out));
  Button button_8 (.out(button_8_out));
  LED led_11 (.in(nor_11_out));
  nor nor_11 (nor_11_out, C0, D1);
  D_Flip_Flop d_ff_4 (.clk(button_3_out), .D(C0), .Q(C1), .Qn(D1), .reset(button_4_out));  // open: preset
  LED led_12 (.in(nor_12_out));
  nor nor_12 (nor_12_out, F0, F2);
  D_Flip_Flop d_ff_5 (.clk(button_5_out), .D(E0), .Q(E1), .Qn(F1), .reset(button_6_out));  // open: preset
  LED led_13 (.in(nor_13_out));
  nor nor_13 (nor_13_out, L1, K2);
  D_Flip_Flop d_ff_6 (.clk(button_7_out), .D(L5), .Q(K0), .Qn(L0), .reset(button_8_out));  // open: preset
  LED led_14 (.in(nor_14_out));
  nor nor_14 (nor_14_out, I0, I4);
  Button button_9 (.out(button_9_out));
  Button button_10 (.out(button_10_out));
  LED led_15 (.in(nor_15_out));
  LED led_16 (.in(nor_16_out));
  nor nor_15 (nor_15_out, E0, F1);
  nor nor_16 (nor_16_out, E1, F2);
  D_Flip_Flop d_ff_7 (.clk(button_5_out), .D(E1), .Q(E2), .Qn(F2), .reset(button_6_out));  // open: preset
  LED led_17 (.in(nor_17_out));
  nor nor_17 (nor_17_out, L2, K3);
  D_Flip_Flop d_ff_8 (.clk(button_7_out), .D(K0), .Q(K1), .Qn(L1), .reset(button_8_out));  // open: preset
  LED led_18 (.in(nor_18_out));
  nor nor_18 (nor_18_out, J0, I1);
  D_Flip_Flop d_ff_9 (.clk(button_9_out), .D(J4), .Q(I0), .Qn(J0), .reset(button_10_out));  // open: preset
  LED led_19 (.in(nor_19_out));
  LED led_20 (.in(nor_20_out));
  nor nor_19 (nor_19_out, L3, K4);
  nor nor_20 (nor_20_out, L4, K5);
  LED led_21 (.in(nor_21_out));
  LED led_22 (.in(nor_22_out));
  nor nor_21 (nor_21_out, J1, I2);
  nor nor_22 (nor_22_out, J2, I3);
  LED led_23 (.in(nor_23_out));
  LED led_24 (.in(nor_24_out));
  nor nor_23 (nor_23_out, G0, G3);
  nor nor_24 (nor_24_out, H0, G1);
  Button button_11 (.out(button_11_out));
  Button button_12 (.out(button_12_out));
  LED led_25 (.in(nor_25_out));
  nor nor_25 (nor_25_out, L0, L5);
  D_Flip_Flop d_ff_10 (.clk(button_7_out), .D(K1), .Q(K2), .Qn(L2), .reset(button_8_out));  // open: preset
  LED led_26 (.in(nor_26_out));
  nor nor_26 (nor_26_out, J3, I4);
  D_Flip_Flop d_ff_11 (.clk(button_9_out), .D(I0), .Q(I1), .Qn(J1), .reset(button_10_out));  // open: preset
  LED led_27 (.in(nor_27_out));
  nor nor_27 (nor_27_out, H1, G2);
  D_Flip_Flop d_ff_12 (.clk(button_11_out), .D(H3), .Q(G0), .Qn(H0), .reset(button_12_out));  // open: preset
  LED led_28 (.in(nor_28_out));
  nor nor_28 (nor_28_out, K0, L1);
  D_Flip_Flop d_ff_13 (.clk(button_7_out), .D(K2), .Q(K3), .Qn(L3), .reset(button_8_out));  // open: preset
  LED led_29 (.in(nor_29_out));
  nor nor_29 (nor_29_out, J0, J4);
  D_Flip_Flop d_ff_14 (.clk(button_9_out), .D(I1), .Q(I2), .Qn(J2), .reset(button_10_out));  // open: preset
  LED led_30 (.in(nor_30_out));
  nor nor_30 (nor_30_out, H2, G3);
  D_Flip_Flop d_ff_15 (.clk(button_11_out), .D(G0), .Q(G1), .Qn(H1), .reset(button_12_out));  // open: preset
  LED led_31 (.in(nor_31_out));
  LED led_32 (.in(nor_32_out));
  nor nor_31 (nor_31_out, K1, L2);
  nor nor_32 (nor_32_out, K2, L3);
  D_Flip_Flop d_ff_16 (.clk(button_7_out), .D(K3), .Q(K4), .Qn(L4), .reset(button_8_out));  // open: preset
  LED led_33 (.in(nor_33_out));
  LED led_34 (.in(nor_34_out));
  nor nor_33 (nor_33_out, I0, J1);
  nor nor_34 (nor_34_out, I1, J2);
  D_Flip_Flop d_ff_17 (.clk(button_9_out), .D(I2), .Q(I3), .Qn(J3), .reset(button_10_out));  // open: preset
  LED led_35 (.in(nor_35_out));
  LED led_36 (.in(nor_36_out));
  nor nor_35 (nor_35_out, H0, H3);
  nor nor_36 (nor_36_out, G0, H1);
  D_Flip_Flop d_ff_18 (.clk(button_11_out), .D(G1), .Q(G2), .Qn(H2), .reset(button_12_out));  // open: preset
  LED led_37 (.in(nor_37_out));
  nor nor_37 (nor_37_out, K3, L4);
  LED led_38 (.in(nor_38_out));
  nor nor_38 (nor_38_out, I2, J3);
  LED led_39 (.in(nor_39_out));
  nor nor_39 (nor_39_out, G1, H2);
  LED led_40 (.in(nor_40_out));
  nor nor_40 (nor_40_out, K4, L5);
  D_Flip_Flop d_ff_19 (.clk(button_7_out), .D(K4), .Q(K5), .Qn(L5), .reset(button_8_out));  // open: preset
  LED led_41 (.in(nor_41_out));
  nor nor_41 (nor_41_out, I3, J4);
  D_Flip_Flop d_ff_20 (.clk(button_9_out), .D(I3), .Q(I4), .Qn(J4), .reset(button_10_out));  // open: preset
  LED led_42 (.in(nor_42_out));
  nor nor_42 (nor_42_out, G2, H3);
  D_Flip_Flop d_ff_21 (.clk(button_11_out), .D(G2), .Q(G3), .Qn(H3), .reset(button_12_out));  // open: preset
endmodule
