// Logisim project DigitalDice.circ as structural Verilog: 1 circuit, main circuit main
module main (
);

  wire button_1_out, button_2_out, D0, D1, D2, D3, R, R0, R1, R2, S, S0, S1, S2;

  Button button_1 (.out(button_1_out));
  Button button_2 (.out(button_2_out));
  LED led_1 (.in(D1));
  LED led_2 (.in(D2));
  LED #(.active("false")) led_3 (.in(D3));
  LED #(.active("false")) led_4 (.in(D3));
  LED led_5 (.in(D0));
  LED led_6 (.in(D2));
  LED led_7 (.in(D1));
  D_Flip_Flop d_ff_1 (.clk(button_1_out), .D(R), .Q(S), .Qn(R), .reset(button_2_out));  // open: preset
  D_Flip_Flop d_ff_2 (.clk(button_1_out), .D(R2), .Q(S0), .Qn(R0), .reset(button_2_out));  // open: preset
  LED led_8 (.in(D0));
  LED led_9 (.in(D1));
  nand nand_1 (D0, S, S);
  nand nand_2 (D1, R2, R0);
  D_Flip_Flop d_ff_3 (.clk(button_1_out), .D(S0), .Q(S1), .Qn(R1), .reset(button_2_out));  // open: preset
  LED led_10 (.in(D2));
  LED #(.active("false")) led_11 (.in(D3));
  nand nand_3 (D2, R2, R2);
  nand nand_4 (D3, R1, S2);
  D_Flip_Flop d_ff_4 (.clk(button_1_out), .D(S1), .Q(S2), .Qn(R2), .reset(button_2_out));  // open: preset
endmodule
