// Logisim project Jokenpo.circ as structural Verilog: 1 circuit, main circuit main
module main (
  input  in_1,
  input  in_2,
  input  in_3,
  input  in_4,
  input  in_5,
  input  in_6,
  input  in_7,
  input  in_8
);

  wire and_1_out, and_2_out, CLK, clock_1_out, CLR, D0, D1, D2, D3, Draw, E1, E2, EN, KEN, not_1_out,
       not_2_out, or_1_out, P1, P2, PA_1, PA_2, PE_1, PE_2, Q0, q0_t, Q1, q1_t, SD0, SD1, SD2, SD3, TE_1,
       TE_2, xnor_1_out, xnor_2_out, xnor_3_out, xnor_4_out;

  LED led_1 (.in(PE_1));
  LED led_2 (.in(CLR));
  LED led_3 (.in(PE_2));
  LED led_4 (.in(PA_1));
  LED led_5 (.in(KEN));
  LED led_6 (.in(PA_2));
  nor nor_1 (EN, Q1, Q0);
  and and_1 (and_1_out, in_4, in_8);
  Decoder #(.enable("false"), .select(2)) decoder_1 (
    .out1(PA_1), .out2(PE_1), .out3(TE_1), .sel({SD1, SD0}));  // open: out0
  LED led_7 (.in(TE_1));
  LED led_8 (.in(CLK));
  LED led_9 (.in(TE_2));
  nor nor_2 (CLR, Q1, q0_t);
  Clock clock_1 (.out(clock_1_out));
  not not_1 (not_1_out, EN);
  xnor xnor_1 (xnor_1_out, in_1, in_3);
  xnor xnor_2 (xnor_2_out, in_2, in_3);
  and and_2 (and_2_out, clock_1_out, not_1_out);
  or or_1 (or_1_out, and_2_out, and_1_out);
  nor nor_3 (D1, xnor_1_out, in_2);
  nor nor_4 (D0, xnor_2_out, in_1);
  LED led_10 (.in(P1));
  LED led_11 (.in(Draw));
  LED led_12 (.in(P2));
  nor nor_5 (KEN, q1_t, q0_t);
  D_Flip_Flop d_ff_1 (.clk(or_1_out), .D(q1_t), .Q(Q0), .Qn(q0_t));  // open: preset, reset
  Decoder #(.enable("false"), .select(2)) decoder_2 (
    .out1(PA_2), .out2(PE_2), .out3(TE_2), .sel({SD3, SD2}));  // open: out0
  LED led_13 (.in(E1));
  LED led_14 (.in(E2));
  xnor xnor_3 (xnor_3_out, in_5, in_7);
  xnor xnor_4 (xnor_4_out, in_6, in_7);
  nor nor_6 (CLK, q1_t, Q0);
  D_Flip_Flop d_ff_2 (.clk(or_1_out), .D(Q0), .Q(Q1), .Qn(q1_t));  // open: preset, reset
  nor nor_7 (D3, xnor_3_out, in_6);
  nor nor_8 (D2, xnor_4_out, in_5);
  D_Flip_Flop d_ff_3 (.clk(not_2_out), .D(D0), .Q(SD0), .reset(CLR));  // open: Qn, preset
  D_Flip_Flop d_ff_4 (.clk(not_2_out), .D(D1), .Q(SD1), .reset(CLR));  // open: Qn, preset
  D_Flip_Flop d_ff_5 (.clk(not_2_out), .D(D2), .Q(SD2), .reset(CLR));  // open: Qn, preset
  D_Flip_Flop d_ff_6 (.clk(not_2_out), .D(D3), .Q(SD3), .reset(CLR));  // open: Qn, preset
  not not_2 (not_2_out, CLK);
  Decoder #(.enable("false"), .select(4)) decoder_3 (
    .out1(E1), .out2(E1), .out3(E1), .out4(E2), .out5(Draw), .out6(P2), .out7(P1), .out8(E2), .out9(P1),
    .out10(Draw), .out11(P2), .out12(E2), .out13(P2), .out14(P1), .out15(Draw), .sel({SD3, SD2, SD1, SD0}));  // open: out0

  // Other names for the same wires on the sheet: JO = CLR; PA_P1 = in_2; PA_P2 = in_6; PE_P1 = in_1; PE_P2 = in_5;
  //   PO = CLK; RS_P1 = in_4; RS_P2 = in_8; TE_P1 = in_3; TE_P2 = in_7
endmodule
