// Logisim project UniversalGates.circ as structural Verilog: 1 circuit, main circuit main
module main (
  input  in_1,
  input  in_2,
  input  in_3,
  input  in_4,
  input  in_5,
  input  in_6,
  input  in_7,
  input  in_8,
  input  in_9,
  input  in_10,
  input  in_11,
  input  in_12,
  input  in_13,
  input  in_14,
  input  in_15,
  input  in_16,
  input  in_17,
  input  in_18,
  input  in_19,
  input  in_20,
  input  in_21,
  input  in_22,
  input  in_23,
  input  in_24,
  input  in_25,
  input  in_26,
  input  in_27,
  input  in_28,
  input  in_29,
  input  in_30,
  input  in_31,
  input  in_32,
  input  in_33,
  input  in_34,
  input  in_35,
  input  in_36,
  input  in_37,
  input  in_38,
  input  in_39,
  input  in_40,
  input  in_41,
  input  in_42
);

  wire and_1_out, buffer_1_out, nand_1_out, nand_2_out, nand_3_out, nand_4_out, nand_5_out, nand_6_out,
       nand_7_out, nand_8_out, nand_9_out, nand_10_out, nand_11_out, nand_12_out, nand_13_out, nand_14_out,
       nand_15_out, nand_16_out, nand_17_out, nand_18_out, nand_19_out, nand_20_out, nand_21_out,
       nand_22_out, nand_23_out, nor_1_out, nor_2_out, nor_3_out, nor_4_out, nor_5_out, nor_6_out, nor_7_out,
       nor_8_out, nor_9_out, nor_10_out, nor_11_out, nor_12_out, nor_13_out, nor_14_out, nor_15_out,
       nor_16_out, nor_17_out, nor_18_out, nor_19_out, nor_20_out, nor_21_out, nor_22_out, nor_23_out,
       not_1_out, or_1_out, xnor_1_out, xor_1_out;

  nand nand_1 (nand_1_out, in_37, in_41);
  nand nand_2 (nand_2_out, in_13, in_13);
  nand nand_3 (nand_3_out, in_18, in_18);
  nand nand_4 (nand_4_out, in_31, in_35);
  nand nand_5 (nand_5_out, in_37, nand_1_out);
  nand nand_6 (nand_6_out, nand_1_out, in_41);
  nand nand_7 (nand_7_out, in_1, in_1);
  nand nand_8 (nand_8_out, in_7, in_7);
  nand nand_9 (nand_9_out, in_12, in_12);
  nand nand_10 (nand_10_out, nand_2_out, nand_3_out);
  nand nand_11 (nand_11_out, in_20, in_22);
  nand nand_12 (nand_12_out, in_31, nand_4_out);
  nand nand_13 (nand_13_out, nand_4_out, in_35);
  nand nand_14 (nand_14_out, nand_5_out, nand_6_out);
  nand nand_15 (nand_15_out, nand_7_out, nand_7_out);
  LED led_1 (.in(nand_15_out));
  nand nand_16 (nand_16_out, in_4, in_4);
  LED led_2 (.in(nand_16_out));
  nand nand_17 (nand_17_out, nand_8_out, nand_9_out);
  LED led_3 (.in(nand_17_out));
  nand nand_18 (nand_18_out, nand_10_out, nand_10_out);
  LED led_4 (.in(nand_18_out));
  nand nand_19 (nand_19_out, nand_11_out, nand_11_out);
  LED led_5 (.in(nand_19_out));
  nand nand_20 (nand_20_out, in_26, in_28);
  LED led_6 (.in(nand_20_out));
  nand nand_21 (nand_21_out, nand_12_out, nand_13_out);
  LED led_7 (.in(nand_21_out));
  nand nand_22 (nand_22_out, nand_14_out, nand_14_out);
  LED led_8 (.in(nand_22_out));
  buf buffer_1 (buffer_1_out, in_2);
  LED led_9 (.in(buffer_1_out));
  not not_1 (not_1_out, in_5);
  LED led_10 (.in(not_1_out));
  or or_1 (or_1_out, in_8, in_10);
  nor nor_1 (nor_1_out, in_14, in_16);
  and and_1 (and_1_out, in_21, in_23);
  nand nand_23 (nand_23_out, in_27, in_29);
  xor xor_1 (xor_1_out, in_33, in_34);
  LED led_11 (.in(or_1_out));
  LED led_12 (.in(nor_1_out));
  LED led_13 (.in(and_1_out));
  LED led_14 (.in(nand_23_out));
  LED led_15 (.in(xor_1_out));
  xnor xnor_1 (xnor_1_out, in_39, in_40);
  LED led_16 (.in(xnor_1_out));
  nor nor_2 (nor_2_out, in_3, in_3);
  nor nor_3 (nor_3_out, in_6, in_6);
  nor nor_4 (nor_4_out, in_9, in_11);
  nor nor_5 (nor_5_out, in_15, in_17);
  nor nor_6 (nor_6_out, in_19, in_19);
  nor nor_7 (nor_7_out, in_24, in_24);
  nor nor_8 (nor_8_out, in_25, in_25);
  nor nor_9 (nor_9_out, in_30, in_30);
  nor nor_10 (nor_10_out, in_32, in_36);
  nor nor_11 (nor_11_out, in_38, in_42);
  nor nor_12 (nor_12_out, nor_2_out, nor_2_out);
  LED led_17 (.in(nor_12_out));
  LED led_18 (.in(nor_3_out));
  nor nor_13 (nor_13_out, nor_4_out, nor_4_out);
  LED led_19 (.in(nor_13_out));
  LED led_20 (.in(nor_5_out));
  nor nor_14 (nor_14_out, nor_6_out, nor_7_out);
  LED led_21 (.in(nor_14_out));
  nor nor_15 (nor_15_out, nor_8_out, nor_9_out);
  nor nor_16 (nor_16_out, in_32, nor_10_out);
  nor nor_17 (nor_17_out, nor_10_out, in_36);
  nor nor_18 (nor_18_out, in_38, nor_11_out);
  nor nor_19 (nor_19_out, nor_11_out, in_42);
  nor nor_20 (nor_20_out, nor_15_out, nor_15_out);
  LED led_22 (.in(nor_20_out));
  nor nor_21 (nor_21_out, nor_16_out, nor_17_out);
  nor nor_22 (nor_22_out, nor_18_out, nor_19_out);
  LED led_23 (.in(nor_22_out));
  nor nor_23 (nor_23_out, nor_21_out, nor_21_out);
  LED led_24 (.in(nor_23_out));
endmodule
