// Logisim project ZigZagEffect.circ as structural Verilog: 1 circuit, main circuit main
module main (
);

  wire clock_1_out, D, multiplexer_1_out, multiplexer_2_out, multiplexer_3_out, nor_1_out, nor_4_out,
       nor_5_out, nor_6_out, nor_7_out, R, R0, R1, R2, S, S0, S1, S2;

  Clock clock_1 (.out(clock_1_out));
  nor nor_1 (nor_1_out, S, D);
  nor nor_2 (D, nor_1_out, R);
  Multiplexer multiplexer_1 (.in0(R2), .in1(S1), .out(multiplexer_1_out), .sel(D));
  D_Flip_Flop d_ff_1 (.clk(clock_1_out), .D(multiplexer_1_out), .Q(S0), .Qn(R0));  // open: preset, reset
  LED led_1 (.in(R));
  LED led_2 (.in(nor_4_out));
  nor nor_3 (R, S0, S2);
  nor nor_4 (nor_4_out, R0, S1);
  Multiplexer multiplexer_2 (.in0(S0), .in1(S2), .out(multiplexer_2_out), .sel(D));
  LED led_3 (.in(nor_5_out));
  nor nor_5 (nor_5_out, R1, S2);
  D_Flip_Flop d_ff_2 (.clk(clock_1_out), .D(multiplexer_2_out), .Q(S1), .Qn(R1));  // open: preset, reset
  LED led_4 (.in(nor_6_out));
  LED led_5 (.in(nor_7_out));
  nor nor_6 (nor_6_out, R0, R2);
  nor nor_7 (nor_7_out, S0, R1);
  Multiplexer multiplexer_3 (.in0(S1), .in1(R0), .out(multiplexer_3_out), .sel(D));
  LED led_6 (.in(S));
  nor nor_8 (S, S1, R2);
  D_Flip_Flop d_ff_3 (.clk(clock_1_out), .D(multiplexer_3_out), .Q(S2), .Qn(R2));  // open: preset, reset
endmodule
